// Logisim project project.circ as structural Verilog: 5 circuits, main circuit Project
module Project (
);

  wire branch, Clock, comparison, dataMemRead, dataMemWrite, jump, or_1_out, regWrite, Reset;
  wire [1:0] ALUcontrol;
  wire [3:0] DEST_SRC_OP1, multiplexer_2_out, SRC1_OP2, SRC2;
  wire [9:0] LD_ST_Address;
  wire [17:0] ALUresult, dataMemResult, JumpAddress, multiplexer_1_out, program_counter_1_output, REG1_data,
       REG2_data, REG2_data_new, rom_1_data;

  Button button_1 (.out(Reset));
  Clock clock_1 (.out(Clock));
  Program_Counter program_counter_1 (
    .jump(jump), .branch(branch), .reset(Reset), .JumpAddress(JumpAddress), .BranchAddress(REG2_data_new),
    .\output (program_counter_1_output), .clock(Clock));
  ALU alu_1 (.Data_1(REG1_data), .Data_2(REG2_data_new), .ALU_Result(ALUresult), .ALUcontrol(ALUcontrol));
  ROM #(.addrWidth(18), .dataWidth(18)) rom_1 (.addr(program_counter_1_output), .data(rom_1_data));  // open: sel
  or or_1 (or_1_out, dataMemWrite, comparison);
  Control_Unit control_unit_1 (
    .Instruction(rom_1_data), .Register_1(REG1_data), .Register_2(REG2_data), .ALUcontrol(ALUcontrol),
    .SRC2(SRC2), .regWrite(regWrite), .SRC1_OP2(SRC1_OP2), .DEST_SRC_OP1(DEST_SRC_OP1),
    .dataMemRead(dataMemRead), .dataMemWrite(dataMemWrite), .jump(jump), .branch(branch),
    .REG2_data_new(REG2_data_new), .LD_ST_ADDRESS(LD_ST_Address), .JumpAddress(JumpAddress),
    .comparison(comparison));
  Multiplexer #(.width(18), .enable("false")) multiplexer_1 (
    .in0(ALUresult), .in1(dataMemResult), .out(multiplexer_1_out), .sel(dataMemRead));
  Multiplexer #(.width(4), .enable("false")) multiplexer_2 (
    .in0(SRC2), .in1(DEST_SRC_OP1), .out(multiplexer_2_out), .sel(or_1_out));
  Register_File register_file_1 (
    .Write_Data(multiplexer_1_out), .Clock(Clock), .Enable_Write(regWrite), .Read_Register_1(SRC1_OP2),
    .Read_Register_2(multiplexer_2_out), .Read_Data_1(REG1_data), .Read_Data_2(REG2_data),
    .Write_Address(DEST_SRC_OP1));
  RAM #(.addrWidth(10), .dataWidth(18), .bus("separate")) ram_1 (
    .addr(LD_ST_Address), .din(REG2_data_new), .data(dataMemResult), .str(dataMemWrite), .sel(1'b1),
    .clk(Clock), .ld(dataMemRead));  // open: clr

  // Notes on the sheet:
  //   Check if ST or comparison
endmodule

module Register_File (
  input  [3:0] Write_Address,
  input  [17:0] Write_Data,
  input  Clock,
  input  Enable_Write,
  input  [3:0] Read_Register_1,
  input  [3:0] Read_Register_2,
  output [17:0] Read_Data_1,
  output [17:0] Read_Data_2
);

  wire _0, _1, _2, _3, _4, _5, _6, _7, _8, _9, _10, _11, _12, _13, _14, _15, and_1_out, and_2_out, and_3_out,
       and_4_out, and_5_out, and_6_out, and_7_out, and_8_out, and_9_out, and_10_out, and_11_out, and_12_out,
       and_13_out, and_14_out, and_15_out, and_16_out;
  wire [17:0] Q0, Q1, Q2, Q3, Q4, Q5, Q6, Q7, Q8, Q9, Q10, Q11, Q12, Q13, Q14, Q15;

  Decoder #(.select(4), .enable("false")) decoder_1 (
    .out0(_0), .out1(_1), .out2(_2), .out3(_3), .out4(_4), .out5(_5), .out6(_6), .out7(_7), .out8(_8),
    .out9(_9), .out10(_10), .out11(_11), .out12(_12), .out13(_13), .out14(_14), .out15(_15),
    .sel(Write_Address));
  and and_1 (and_1_out, _0, Enable_Write);
  and and_2 (and_2_out, _1, Enable_Write);
  and and_3 (and_3_out, _2, Enable_Write);
  and and_4 (and_4_out, _3, Enable_Write);
  and and_5 (and_5_out, _4, Enable_Write);
  and and_6 (and_6_out, _5, Enable_Write);
  and and_7 (and_7_out, _6, Enable_Write);
  and and_8 (and_8_out, _7, Enable_Write);
  Register #(.width(18)) register_1 (.D(Write_Data), .en(and_1_out), .Q(Q0), .clk(Clock));  // open: clr
  Register #(.width(18)) register_2 (.D(Write_Data), .en(and_2_out), .Q(Q1), .clk(Clock));  // open: clr
  Register #(.width(18)) register_3 (.D(Write_Data), .en(and_3_out), .Q(Q2), .clk(Clock));  // open: clr
  Register #(.width(18)) register_4 (.D(Write_Data), .en(and_4_out), .Q(Q3), .clk(Clock));  // open: clr
  Register #(.width(18)) register_5 (.D(Write_Data), .en(and_5_out), .Q(Q4), .clk(Clock));  // open: clr
  Register #(.width(18)) register_6 (.D(Write_Data), .en(and_6_out), .Q(Q5), .clk(Clock));  // open: clr
  Register #(.width(18)) register_7 (.D(Write_Data), .en(and_7_out), .Q(Q6), .clk(Clock));  // open: clr
  Register #(.width(18)) register_8 (.D(Write_Data), .en(and_8_out), .Q(Q7), .clk(Clock));  // open: clr
  and and_9 (and_9_out, _8, Enable_Write);
  and and_10 (and_10_out, _9, Enable_Write);
  and and_11 (and_11_out, _10, Enable_Write);
  and and_12 (and_12_out, _11, Enable_Write);
  and and_13 (and_13_out, _12, Enable_Write);
  and and_14 (and_14_out, _13, Enable_Write);
  and and_15 (and_15_out, _14, Enable_Write);
  and and_16 (and_16_out, _15, Enable_Write);
  Register #(.width(18)) register_9 (.D(Write_Data), .en(and_9_out), .Q(Q8), .clk(Clock));  // open: clr
  Register #(.width(18)) register_10 (.D(Write_Data), .en(and_10_out), .Q(Q9), .clk(Clock));  // open: clr
  Register #(.width(18)) register_11 (.D(Write_Data), .en(and_11_out), .Q(Q10), .clk(Clock));  // open: clr
  Register #(.width(18)) register_12 (.D(Write_Data), .en(and_12_out), .Q(Q11), .clk(Clock));  // open: clr
  Register #(.width(18)) register_13 (.D(Write_Data), .en(and_13_out), .Q(Q12), .clk(Clock));  // open: clr
  Register #(.width(18)) register_14 (.D(Write_Data), .en(and_14_out), .Q(Q13), .clk(Clock));  // open: clr
  Register #(.width(18)) register_15 (.D(Write_Data), .en(and_15_out), .Q(Q14), .clk(Clock));  // open: clr
  Register #(.width(18)) register_16 (.D(Write_Data), .en(and_16_out), .Q(Q15), .clk(Clock));  // open: clr
  Multiplexer #(.select(4), .width(18), .enable("false")) multiplexer_1 (
    .in0(Q0), .in1(Q1), .in2(Q2), .in3(Q3), .in4(Q4), .in5(Q5), .in6(Q6), .in7(Q7), .in8(Q8), .in9(Q9),
    .in10(Q10), .in11(Q11), .in12(Q12), .in13(Q13), .in14(Q14), .in15(Q15), .out(Read_Data_1),
    .sel(Read_Register_1));
  Multiplexer #(.select(4), .width(18), .enable("false")) multiplexer_2 (
    .in0(Q0), .in1(Q1), .in2(Q2), .in3(Q3), .in4(Q4), .in5(Q5), .in6(Q6), .in7(Q7), .in8(Q8), .in9(Q9),
    .in10(Q10), .in11(Q11), .in12(Q12), .in13(Q13), .in14(Q14), .in15(Q15), .out(Read_Data_2),
    .sel(Read_Register_2));

  // Other names for the same wires on the sheet: C = Clock; R1[3:0] = Read_Register_1; R2[3:0] = Read_Register_2;
  //   RW = Enable_Write; WD[17:0] = Write_Data

  // Notes on the sheet:
  //   Decode write address
  //   Register File
endmodule

module Control_Unit (
  input  [17:0] Instruction,
  input  [17:0] Register_1,
  input  [17:0] Register_2,
  output [17:0] JumpAddress,
  output [9:0] LD_ST_ADDRESS,
  output [1:0] ALUcontrol,
  output regWrite,
  output [3:0] SRC2,
  output [3:0] SRC1_OP2,
  output [3:0] DEST_SRC_OP1,
  output comparison,
  output branch,
  output dataMemRead,
  output dataMemWrite,
  output jump,
  output [17:0] REG2_data_new
);

  wire ADD, ADDI, AND, and_1_out, and_2_out, and_3_out, and_4_out, and_5_out, ANDI, BEQ, BGE, BGT, BLE, BLT,
       comparator_1_eq, comparator_1_gt, comparator_1_lt, immediate, OR, or_1_out, or_2_out, or_3_out,
       or_4_out, or_5_out, or_8_out, ORI, XOR, XORI;
  wire [17:0] bit_extender_2_out;

  Decoder #(.select(4), .enable("false")) decoder_1 (
    .out0(ADD), .out1(AND), .out2(OR), .out3(XOR), .out4(ADDI), .out5(ANDI), .out6(ORI), .out7(XORI),
    .out8(dataMemRead), .out9(dataMemWrite), .out10(jump), .out11(BEQ), .out12(BLT), .out13(BGT),
    .out14(BLE), .out15(BGE), .sel(Instruction[17:14]));
  assign JumpAddress = {{4{Instruction[13]}}, Instruction[13:0]};  // Bit_Extender bit_extender_1
  Comparator #(.width(18)) comparator_1 (
    .a(Register_2), .b(Register_1), .gt(comparator_1_gt), .eq(comparator_1_eq), .lt(comparator_1_lt));
  or or_1 (or_1_out, AND, ANDI);
  or or_2 (or_2_out, OR, ORI);
  or or_3 (or_3_out, XOR, XORI);
  or or_4 (or_4_out, comparator_1_eq, comparator_1_gt);
  or or_5 (or_5_out, comparator_1_lt, comparator_1_eq);
  or or_6 (ALUcontrol[0], or_2_out, or_3_out);
  or or_7 (ALUcontrol[1], or_1_out, or_3_out);
  and and_1 (and_1_out, or_4_out, BGE);
  and and_2 (and_2_out, BGT, comparator_1_gt);
  and and_3 (and_3_out, BEQ, comparator_1_eq);
  and and_4 (and_4_out, BLT, comparator_1_lt);
  and and_5 (and_5_out, BLE, or_5_out);
  Multiplexer #(.width(18), .enable("false")) multiplexer_1 (
    .in0(Register_2), .in1(bit_extender_2_out), .out(REG2_data_new), .sel(or_8_out));
  assign bit_extender_2_out = {{12{Instruction[5]}}, Instruction[5:0]};  // Bit_Extender bit_extender_2
  or or_8 (or_8_out, immediate, comparison);
  or or_9 (immediate, ANDI, ORI, XORI, ADDI);
  or or_10 (branch, and_1_out, and_2_out, and_3_out, and_4_out, and_5_out);
  or or_11 (regWrite, ADD, AND, OR, XOR, ADDI, ANDI, ORI, XORI, dataMemRead);
  or or_12 (comparison, BEQ, BLT, BGT, BLE, BGE);

  assign DEST_SRC_OP1 = Instruction[13:10];
  assign LD_ST_ADDRESS = Instruction[9:0];
  assign SRC1_OP2 = Instruction[9:6];
  assign SRC2 = Instruction[5:2];

  // Other names for the same wires on the sheet: IMMEDIATE_ADDRESS_6[5:0] = Instruction[5:0]; LD = dataMemRead;
  //   ST = dataMemWrite

  // Notes on the sheet:
  //   Decode Opeartion
  //   Decode addresses and SRC/DEST/OP
  //   Compare 2 registers and branch according to result
  //   Choose ALU operation
  //   ADD/ADDI 00 - AND/ANDI 10 - ORR/ORRI 01 - XOR/XORI 11
  //   Choose register_2 data or immediate data
  //   Check if any immediate value exist
  //   any writing to register exists
endmodule

module ALU (
  input  [17:0] Data_1,
  input  [17:0] Data_2,
  input  [1:0] ALUcontrol,
  output [17:0] ALU_Result
);

  wire [17:0] adder_1_out, and_1_out, or_1_out, xor_1_out;

  Adder #(.width(18)) adder_1 (.a(Data_1), .b(Data_2), .out(adder_1_out));  // open: cin, cout
  assign or_1_out = Data_1 | Data_2;  // OR_Gate or_1, 18 bits wide
  assign and_1_out = Data_1 & Data_2;  // AND_Gate and_1, 18 bits wide
  assign xor_1_out = Data_1 ^ Data_2;  // XOR_Gate xor_1, 18 bits wide
  Multiplexer #(.select(2), .width(18), .enable("false")) multiplexer_1 (
    .in0(adder_1_out), .in1(or_1_out), .in2(and_1_out), .in3(xor_1_out), .out(ALU_Result), .sel(ALUcontrol));
endmodule

module Program_Counter (
  input  jump,
  input  branch,
  input  clock,
  input  reset,
  input  [17:0] JumpAddress,
  input  [17:0] BranchAddress,
  output [17:0] \output 
);

  wire not_1_out, or_1_out;
  wire [17:0] controlled_buffer_1_out, multiplexer_1_out, result;

  or or_1 (or_1_out, jump, branch);
  not not_1 (not_1_out, or_1_out);
  Counter #(.width(18), .max('h3ffff)) counter_1 (
    .load(or_1_out), .D(result), .count(not_1_out), .Q(\output ), .clk(clock), .clr(reset));  // open: carry
  assign controlled_buffer_1_out = branch ? BranchAddress : 18'bz;  // Controlled_Buffer controlled_buffer_1
  Multiplexer #(.width(18), .enable("false")) multiplexer_1 (
    .in0(controlled_buffer_1_out), .in1(JumpAddress), .out(multiplexer_1_out), .sel(jump));
  Adder #(.width(18)) adder_1 (.a(\output ), .b(multiplexer_1_out), .out(result));  // open: cin, cout
endmodule
